# Fritzing sketch led6 (saved by Fritzing 0.9.2b)
circuit board: 5.53292cm x 6.82532cm
breadboards: 1

parts:
  R1 = Resistor [tolerance=±5% resistance=6.8k package=THT]
  R3 = Resistor [tolerance=±5% resistance=6.8k package=THT]
  R5 = Resistor [tolerance=±5% resistance=6.8k package=THT]
  LED2' = LED - 5mm [color="Red (633nm)" package="5 mm [THT]"]
  LED2 = LED - 5mm [color="Red (633nm)" package="5 mm [THT]"]
  LED1' = LED - 5mm [color="Red (633nm)" package="5 mm [THT]"]
  LED3 = LED - 5mm [color="Red (633nm)" package="5 mm [THT]"]
  LED1 = LED - 5mm [color="Red (633nm)" package="5 mm [THT]"]
  R7 = Resistor [tolerance=±5% resistance=100 package=THT]
  R8 = Resistor [tolerance=±5% resistance=100 package=THT]
  R9 = Resistor [tolerance=±5% resistance=100 package=THT]
  LED3' = LED - 5mm [color="Red (633nm)" package="5 mm [THT]"]
  Q2 = NPN-Transistor [package="TO92 [THT]"]
  Q4 = NPN-Transistor [package="TO92 [THT]"]
  Q6 = NPN-Transistor [package="TO92 [THT]"]
  Q1 = PNP-Transistor [package="TO92 [THT]"]
  Q3 = PNP-Transistor [package="TO92 [THT]"]
  Q5 = PNP-Transistor [package="SOT-23 [SMD]"]

nets:
  N1: R1.Pin_0, Q2.B, Q1.B
  N2: R3.Pin_0, Q4.B, Q3.B
  N3: R5.Pin_0, Q6.B, Q5.0
  N4: LED2'.cathode, LED2.anode, LED1'.anode, LED1.cathode, R8.Pin_0
  N5: LED2'.anode, LED2.cathode, LED3.anode, R9.Pin_0, LED3'.cathode
  N6: LED1'.cathode, LED3.cathode, LED1.anode, R7.Pin_0, LED3'.anode
  N7: R7.Pin_1, Q2.C, Q1.E
  N8: R8.Pin_1, Q4.C, Q3.E
  N9: R9.Pin_1, Q6.C, Q5.2
  5V: Q2.E, Q4.E, Q6.E
  GND: Q1.C, Q3.C, Q5.1

custom parts:
  NPN-Transistor: A standard NPN-transistor
